// Logisim project Domaci2 (2).circ as structural Verilog: 3 circuits, main circuit Obicno
module Obicno (
  input  X1,
  input  X2,
  input  X3,
  input  X4,
  input  X5,
  output Y
);

  wire and_1_out, and_2_out, and_4_out, not_1_out, not_2_out, not_3_out;

  not not_1 (not_1_out, X1);
  not not_2 (not_2_out, X2);
  and and_1 (and_1_out, not_1_out, not_2_out);
  not not_3 (not_3_out, X5);
  and and_2 (and_2_out, and_1_out, X3);
  and and_3 (Y, and_2_out, and_4_out);
  and and_4 (and_4_out, X4, not_3_out);
endmodule

module Celo_NILI (
  input  X1,
  input  X2,
  input  X3,
  input  X4,
  input  X5,
  output Y
);

  wire nor_1_out, nor_2_out, nor_3_out, nor_4_out, nor_5_out, nor_6_out, nor_7_out, nor_8_out, nor_9_out,
       nor_10_out, nor_11_out, nor_12_out, nor_13_out, nor_14_out;

  nor nor_1 (nor_1_out, X1, X1);
  nor nor_2 (nor_2_out, X2, X2);
  nor nor_3 (nor_3_out, X5, X5);
  nor nor_4 (nor_4_out, X4, X4);
  nor nor_5 (nor_5_out, nor_3_out, nor_3_out);
  nor nor_6 (nor_6_out, nor_1_out, nor_1_out);
  nor nor_7 (nor_7_out, nor_2_out, nor_2_out);
  nor nor_8 (nor_8_out, nor_4_out, nor_5_out);
  nor nor_9 (nor_9_out, nor_6_out, nor_7_out);
  nor nor_10 (nor_10_out, nor_9_out, nor_9_out);
  nor nor_11 (nor_11_out, X3, X3);
  nor nor_12 (nor_12_out, nor_10_out, nor_11_out);
  nor nor_13 (nor_13_out, nor_12_out, nor_12_out);
  nor nor_14 (nor_14_out, nor_8_out, nor_8_out);
  nor nor_15 (Y, nor_13_out, nor_14_out);

  // Notes on the sheet:
  //   00110
  //   23.1 : 2+3+1=6 
endmodule

module Skraceno_NILI__domaci (
  input  X1,
  input  X2,
  input  X3,
  input  X4,
  input  X5,
  output Y
);

  wire nor_1_out, nor_2_out, nor_3_out, nor_4_out, nor_5_out, nor_6_out, nor_7_out, nor_8_out;

  nor nor_1 (nor_1_out, X4, X4);
  nor nor_2 (nor_2_out, nor_1_out, X5);
  nor nor_3 (nor_3_out, X1, X2);
  nor nor_4 (nor_4_out, nor_3_out, nor_3_out);
  nor nor_5 (nor_5_out, X3, X3);
  nor nor_6 (nor_6_out, nor_4_out, nor_5_out);
  nor nor_7 (nor_7_out, nor_6_out, nor_6_out);
  nor nor_8 (nor_8_out, nor_2_out, nor_2_out);
  nor nor_9 (Y, nor_7_out, nor_8_out);

  // Notes on the sheet:
  //   00110
  //   23.1 : 2+3+1=6 
endmodule
